# Fritzing sketch main electric draft (saved by Fritzing 0.9.3b)
breadboards: 2

parts:
  Часть1 = Arduino Mega 2560 (Rev3)
  Часть2 = Seeeduino V3.0
  VCC2 = Battery block 9V
  U2 = TRANSCHIPTC5747 [package=camera_sfv24r-2st_2]
  VCC1 = Battery block 9V
  M1 = DC Motor

nets:
  N1: Часть1.5V, M1.pin_2
  N2: Часть1.GND, VCC1.-, M1.pin_1
  N3: Часть1.VIN, VCC1.+
  N4: Часть2.GND, VCC2.-, U2.AGND, U2.AVDD28
  N5: Часть2.VIN, VCC2.+, U2.SCLK
